# Fritzing sketch rpi-rf (saved by Fritzing 0.9.3b)

parts:
  Part1 = RFM9xW
  Raspberry_Pi_1 = Raspberry Pi 3 [part_number=RPI-3-V1.2]

nets:
  N1: Part1.MOSI, Raspberry_Pi_1.GIPO10
  N2: Part1.SCK, Raspberry_Pi_1.GIPO11
  N3: Part1.NSS, Raspberry_Pi_1.GIPO8
  N4: Part1.RESET, Raspberry_Pi_1.GIPO22
  N5: Part1.DIO5, Raspberry_Pi_1.GIPO24
  N6: Part1.GND#9, Raspberry_Pi_1.GND
  VCC: Part1.VCC, Raspberry_Pi_1.3v3
  N7: Part1.DIO0, Raspberry_Pi_1.GIPO25

custom parts:
  RFM9xW: RFM9xW Module connector
