# Fritzing sketch uno-rf (saved by Fritzing 0.9.3b)

parts:
  Part1 = RFM9xW
  Part2 = Arduino Uno (Rev3) - ICSP

nets:
  N1: Part1.MOSI, Part2.D11_PWM/MOSI
  N2: Part1.SCK, Part2.D13/SCK
  N3: Part1.NSS, Part2.D10_PWM/SS
  N4: Part1.RESET, Part2.D9_PWM
  N5: Part1.GND#9, Part2.GND
  VCC: Part1.VCC, Part2.3V3
  N6: Part1.DIO0, Part2.D2

custom parts:
  RFM9xW: RFM9xW Module connector
